// Logisim project control.circ as structural Verilog: 1 circuit, main circuit control_unit
module control_unit (
  input  is32,
  input  LastBit,
  input  Calculate,
  input  clock,
  output Load,
  output Load__Product,
  output ProductAdd,
  output Shift,
  output Clear,
  output LoadMinus
);

  wire and_2_out, and_3_out, and_8_out, and_9_out, and_10_out, and_11_out, and_12_out, and_13_out,
       and_14_out, not_1_out, not_2_out, not_3_out, not_4_out, xor_1_out;
  wire [2:0] or_3_out, State_Register_q;

  not not_1 (not_1_out, State_Register_q[2]);
  not not_2 (not_2_out, State_Register_q[1]);
  not not_3 (not_3_out, State_Register_q[0]);
  xor xor_1 (xor_1_out, State_Register_q[2], State_Register_q[0]);
  not not_4 (not_4_out, LastBit);
  Register #(.width(3)) State_Register (.D(or_3_out), .en(1'b1), .Q(State_Register_q), .clk(clock));  // open: clr
  and and_1 (Load, not_2_out, xor_1_out);
  and and_2 (and_2_out, not_2_out, not_3_out, not_1_out, Calculate);
  and and_3 (and_3_out, not_2_out, not_3_out, State_Register_q[2]);
  and and_4 (ProductAdd, not_1_out, State_Register_q[1], State_Register_q[0]);
  and and_5 (Shift, State_Register_q[2], not_2_out, not_3_out);
  and and_6 (Clear, State_Register_q[2], State_Register_q[1], not_3_out);
  and and_7 (LoadMinus, not_1_out, not_2_out, State_Register_q[0]);
  and and_8 (and_8_out, not_1_out, not_3_out, State_Register_q[1], not_4_out);
  and and_9 (and_9_out, not_2_out, State_Register_q[2], State_Register_q[0], is32);
  and and_10 (and_10_out, State_Register_q[1], State_Register_q[0], not_1_out);
  and and_11 (and_11_out, not_2_out, not_3_out, State_Register_q[2]);
  and and_12 (and_12_out, not_1_out, not_3_out, State_Register_q[1], LastBit);
  and and_13 (and_13_out, not_2_out, State_Register_q[2], State_Register_q[0]);
  and and_14 (and_14_out, not_1_out, not_2_out, State_Register_q[0]);
  or or_1 (Load__Product, ProductAdd, Shift, LoadMinus);
  or or_2 (or_3_out[1], and_12_out, and_13_out, and_14_out);
  or or_3 (or_3_out[0], and_12_out, and_2_out, and_3_out);
  or or_4 (or_3_out[2], and_8_out, and_9_out, and_10_out, and_11_out);

  // Notes on the sheet:
  //   s2
  //   s1
  //   s2'
  //   s1'
  //   s0
  //   s0'
  //   n1
  //   n0
  //   n2
  //   n2
  //   n1
  //   n0
endmodule
