// Logisim project datapath.circ as structural Verilog: 7 circuits, main circuit datapath
module datapath (
  input  [31:0] Multiplicand,
  input  [31:0] Multiplier,
  input  clock,
  input  Load_and_Increment,
  input  SProductAdd,
  input  SShift,
  input  Clear,
  input  LoadMinus,
  input  LoadProduct,
  output PLastBit,
  output [31:0] Product_Low,
  output is32,
  output [31:0] Product_Hi
);

  wire and_1_out, cra_32_bit_1_c_out;
  wire [31:0] _64_bit_shifter_multiplier_output, _64_bit_shifter_product_output, cra_32_bit_1_result,
       multiplexer_1_out, multiplexer_2_out, multiplexer_3_out;

  Multiplexer #(.width(32), .enable("false")) multiplexer_1 (
    .in0(Multiplier), .in1(_64_bit_shifter_multiplier_output), .out(multiplexer_1_out), .sel(SShift));
  Register #(.width(32)) MLierReg (
    .D(multiplexer_1_out), .en(Load_and_Increment), .Q({Product_Low[31:1], PLastBit}), .clk(clock));  // open: clr
  CRA_32_bit cra_32_bit_1 (
    .input1(Multiplicand), .input2(Product_Hi), .c_out(cra_32_bit_1_c_out), .result(cra_32_bit_1_result),
    .cin(1'b0));
  Multiplexer #(.width(32), .enable("false")) multiplexer_2 (
    .in0({32{1'b0}}), .in1(cra_32_bit_1_result), .out(multiplexer_2_out), .sel(SProductAdd));
  Multiplexer #(.width(32), .enable("false")) multiplexer_3 (
    .in0(multiplexer_2_out), .in1(_64_bit_shifter_product_output), .out(multiplexer_3_out), .sel(SShift));
  Counter #(.width(5), .max('h1f)) Counter (
    .load(LoadMinus), .D({5{1'b1}}), .count(1'b1), .carry(is32), .clk(Load_and_Increment), .clr(Clear));  // open: Q
  Register #(.width(32)) ProductReg (
    .D(multiplexer_3_out), .en(LoadProduct), .Q(Product_Hi), .clk(clock));  // open: clr
  and and_1 (and_1_out, cra_32_bit_1_c_out, PLastBit);
  _64_bit_shifter _64_bit_shifter (
    .carry(and_1_out), .Product(Product_Hi), .Multiplier({Product_Low[31:1], PLastBit}),
    .Product_Output(_64_bit_shifter_product_output), .Multiplier_Output(_64_bit_shifter_multiplier_output));

  assign Product_Low[0] = PLastBit;
endmodule

module _64_bit_shifter (
  input  [31:0] Multiplier,
  input  [31:0] Product,
  input  carry,
  output [31:0] Multiplier_Output,
  output [31:0] Product_Output
);


  assign Multiplier_Output = {Product[0], Multiplier[31:1]};
  assign Product_Output = {carry, Product[31:1]};
endmodule

// CRA
module CRA_32_bit (
  input  cin,
  input  [31:0] input1,
  input  [31:0] input2,
  output c_out,
  output [31:0] result
);

  wire cra_4_bit_1_c_out, cra_4_bit_2_c_out, cra_4_bit_3_c_out, cra_4_bit_4_c_out, cra_4_bit_5_c_out,
       cra_4_bit_6_c_out, cra_4_bit_7_c_out;

  CRA_4_bit cra_4_bit_1 (
    .ci(cin), .a0(input1[0]), .b0(input2[0]), .a1(input1[1]), .b1(input2[1]), .a2(input1[2]), .b2(input2[2]),
    .a3(input1[3]), .b3(input2[3]), .s0(result[0]), .s1(result[1]), .s2(result[2]), .s3(result[3]),
    .c_out(cra_4_bit_1_c_out));
  CRA_4_bit cra_4_bit_2 (
    .ci(cra_4_bit_1_c_out), .a0(input1[4]), .b0(input2[4]), .a1(input1[5]), .b1(input2[5]), .a2(input1[6]),
    .b2(input2[6]), .a3(input1[7]), .b3(input2[7]), .s0(result[4]), .s1(result[5]), .s2(result[6]),
    .s3(result[7]), .c_out(cra_4_bit_2_c_out));
  CRA_4_bit cra_4_bit_3 (
    .ci(cra_4_bit_2_c_out), .a0(input1[8]), .b0(input2[8]), .a1(input1[9]), .b1(input2[9]), .a2(input1[10]),
    .b2(input2[10]), .a3(input1[11]), .b3(input2[11]), .s0(result[8]), .s1(result[9]), .s2(result[10]),
    .s3(result[11]), .c_out(cra_4_bit_3_c_out));
  CRA_4_bit cra_4_bit_4 (
    .ci(cra_4_bit_3_c_out), .a0(input1[12]), .b0(input2[12]), .a1(input1[13]), .b1(input2[13]),
    .a2(input1[14]), .b2(input2[14]), .a3(input1[15]), .b3(input2[15]), .s0(result[12]), .s1(result[13]),
    .s2(result[14]), .s3(result[15]), .c_out(cra_4_bit_4_c_out));
  CRA_4_bit cra_4_bit_5 (
    .ci(cra_4_bit_4_c_out), .a0(input1[16]), .b0(input2[16]), .a1(input1[17]), .b1(input2[17]),
    .a2(input1[18]), .b2(input2[18]), .a3(input1[19]), .b3(input2[19]), .s0(result[16]), .s1(result[17]),
    .s2(result[18]), .s3(result[19]), .c_out(cra_4_bit_5_c_out));
  CRA_4_bit cra_4_bit_6 (
    .ci(cra_4_bit_5_c_out), .a0(input1[20]), .b0(input2[20]), .a1(input1[21]), .b1(input2[21]),
    .a2(input1[22]), .b2(input2[22]), .a3(input1[23]), .b3(input2[23]), .s0(result[20]), .s1(result[21]),
    .s2(result[22]), .s3(result[23]), .c_out(cra_4_bit_6_c_out));
  CRA_4_bit cra_4_bit_7 (
    .ci(cra_4_bit_6_c_out), .a0(input1[24]), .b0(input2[24]), .a1(input1[25]), .b1(input2[25]),
    .a2(input1[26]), .b2(input2[26]), .a3(input1[27]), .b3(input2[27]), .s0(result[24]), .s1(result[25]),
    .s2(result[26]), .s3(result[27]), .c_out(cra_4_bit_7_c_out));
  CRA_4_bit cra_4_bit_8 (
    .ci(cra_4_bit_7_c_out), .a0(input1[28]), .b0(input2[28]), .a1(input1[29]), .b1(input2[29]),
    .a2(input1[30]), .b2(input2[30]), .a3(input1[31]), .b3(input2[31]), .s0(result[28]), .s1(result[29]),
    .s2(result[30]), .s3(result[31]), .c_out(c_out));
endmodule

// FA
module Full_Adder_1_bit (
  input  a,
  input  b,
  input  ci,
  output c_out,
  output s
);

  wire and_1_out, and_2_out, and_3_out, xor_1_out;

  and and_1 (and_1_out, a, b);
  and and_2 (and_2_out, a, ci);
  and and_3 (and_3_out, b, ci);
  xor xor_1 (xor_1_out, a, b);
  xor xor_2 (s, xor_1_out, ci);
  or or_1 (c_out, and_1_out, and_2_out, and_3_out);
endmodule

module CRA_4_bit (
  input  ci,
  input  a0,
  input  b0,
  input  a1,
  input  b1,
  input  a2,
  input  b2,
  input  a3,
  input  b3,
  output s0,
  output s1,
  output s2,
  output s3,
  output c_out
);

  wire full_adder_1_bit_1_c_out, full_adder_1_bit_2_c_out, full_adder_1_bit_3_c_out;

  Full_Adder_1_bit full_adder_1_bit_1 (.a(a0), .b(b0), .ci(ci), .c_out(full_adder_1_bit_1_c_out), .s(s0));
  Full_Adder_1_bit full_adder_1_bit_2 (
    .a(a1), .b(b1), .ci(full_adder_1_bit_1_c_out), .c_out(full_adder_1_bit_2_c_out), .s(s1));
  Full_Adder_1_bit full_adder_1_bit_3 (
    .a(a2), .b(b2), .ci(full_adder_1_bit_2_c_out), .c_out(full_adder_1_bit_3_c_out), .s(s2));
  Full_Adder_1_bit full_adder_1_bit_4 (.a(a3), .b(b3), .ci(full_adder_1_bit_3_c_out), .c_out(c_out), .s(s3));
endmodule

module CRA_test (
  input  [31:0] a,
  input  [31:0] b,
  output [31:0] Result,
  output c_out
);

  // Probe on a
  // Probe on b
  CRA_32_bit cra_32_bit_1 (.input1(a), .input2(b), .c_out(c_out), .result(Result), .cin(1'b0));
  // Probe on Result
endmodule

module shifter_test (
  input  [31:0] Product_Left_side,
  input  carry,
  input  [31:0] Multiplier,
  output [31:0] Product_shifted,
  output [31:0] Multiplier_shifted
);

  // Probe on Product_Left_side
  // Probe on Multiplier
  _64_bit_shifter My_shifter (
    .carry(carry), .Product(Product_Left_side), .Multiplier(Multiplier), .Product_Output(Product_shifted),
    .Multiplier_Output(Multiplier_shifted));
  // Probe on Product_shifted
  // Probe on Multiplier_shifted
endmodule
