// Logisim project mult32.circ as structural Verilog: 1 circuit, main circuit main
module main (
  input  [31:0] Multiplier,
  input  [31:0] Multiplicand,
  output [31:0] Result_High,
  output [31:0] Result_Low
);

  wire Calculate_out, clock_1_out, Control_Unit_clear, Control_Unit_load, Control_Unit_load__product,
       Control_Unit_loadminus, Control_Unit_productadd, Control_Unit_shift, Datapath_is32, Datapath_plastbit;

  Button Calculate (.out(Calculate_out));
  Clock clock_1 (.out(clock_1_out));
  // Probe on Multiplier
  control_unit Control_Unit (
    .is32(Datapath_is32), .LastBit(Datapath_plastbit), .Calculate(Calculate_out), .clock(clock_1_out),
    .Load(Control_Unit_load), .ProductAdd(Control_Unit_productadd), .Shift(Control_Unit_shift),
    .Clear(Control_Unit_clear), .LoadMinus(Control_Unit_loadminus), .Load__Product(Control_Unit_load__product));
  // Probe on Multiplicand
  datapath Datapath (
    .Multiplicand(Multiplicand), .Multiplier(Multiplier), .clock(clock_1_out), .PLastBit(Datapath_plastbit),
    .Load_and_Increment(Control_Unit_load), .SProductAdd(Control_Unit_productadd),
    .SShift(Control_Unit_shift), .is32(Datapath_is32), .Clear(Control_Unit_clear),
    .LoadMinus(Control_Unit_loadminus), .Product_Low(Result_Low), .LoadProduct(Control_Unit_load__product),
    .Product_Hi(Result_High));
  // Probe on Result_High
  // Probe on Result_Low

  // Notes on the sheet:
  //   *Enable Clock
  //   *Click Calculate Button
  //   *Change Numbers Click Again
  //   *Enter multiplier and multiplicand numbers
endmodule
